// Logisim project 2sComplementComparator.circ as structural Verilog: 2 circuits, main circuit main
module main (
  input  in_1,
  input  in_2,
  input  A,
  input  in_4,
  input  in_5,
  input  in_6,
  input  B,
  input  in_8,
  input  Constant_1,
  output A___B,
  output A___B_2,
  output A___B_3
);

  wire full_adder_1_carry_out, full_adder_1_sum, full_adder_2_carry_out, full_adder_2_sum,
       full_adder_3_carry_out, full_adder_3_sum, full_adder_4_carry_out, full_adder_4_sum, not_2_out,
       not_3_out, not_5_out, not_6_out, not_7_out, or_1_out, or_2_out, or_3_out, xor_1_out;

  xor xor_1 (xor_1_out, full_adder_1_carry_out, full_adder_2_carry_out);
  Full_Adder full_adder_1 (
    .A(not_3_out), .B(in_1), .Carry_in(full_adder_2_carry_out), .Sum(full_adder_1_sum),
    .Carry_out(full_adder_1_carry_out));
  xor xor_2 (A___B, xor_1_out, full_adder_1_sum);
  Full_Adder full_adder_2 (
    .A(not_2_out), .B(in_2), .Carry_in(full_adder_3_carry_out), .Sum(full_adder_2_sum),
    .Carry_out(full_adder_2_carry_out));
  or or_1 (or_1_out, full_adder_1_sum, full_adder_2_sum, full_adder_3_sum, full_adder_4_sum);
  not not_1 (A___B_2, or_1_out);
  not not_2 (not_2_out, in_6);
  not not_3 (not_3_out, in_5);
  Full_Adder full_adder_3 (
    .A(not_6_out), .B(A), .Carry_in(full_adder_4_carry_out), .Sum(full_adder_3_sum),
    .Carry_out(full_adder_3_carry_out));
  or or_2 (or_2_out, A___B, not_7_out);
  not not_4 (A___B_3, or_2_out);
  not not_5 (not_5_out, in_8);
  not not_6 (not_6_out, B);
  Full_Adder full_adder_4 (
    .A(not_5_out), .B(in_4), .Carry_in(Constant_1), .Sum(full_adder_4_sum), .Carry_out(full_adder_4_carry_out));
  or or_3 (or_3_out, full_adder_1_sum, full_adder_2_sum, full_adder_3_sum, full_adder_4_sum);
  not not_7 (not_7_out, or_3_out);
endmodule

// FA
module Full_Adder (
  input  A,
  input  B,
  input  Carry_in,
  output Sum,
  output Carry_out
);

  wire and_1_out, and_2_out, xor_1_out;

  xor xor_1 (xor_1_out, A, B);
  and and_1 (and_1_out, B, A);
  xor xor_2 (Sum, xor_1_out, Carry_in);
  and and_2 (and_2_out, xor_1_out, Carry_in);
  or or_1 (Carry_out, and_2_out, and_1_out);
endmodule
